// Logisim project project1.circ as structural Verilog
module _7_seg (
  input  A,
  input  B,
  input  C,
  input  D,
  output a_2,
  output e,
  output f,
  output b_2,
  output c_2,
  output g,
  output d_2
);

  wire A_prime, and_1_out, and_2_out, and_3_out, and_4_out, and_5_out, and_6_out, and_7_out, and_8_out,
       and_9_out, and_10_out, and_11_out, and_12_out, and_13_out, and_14_out, and_15_out, and_16_out,
       and_17_out, and_18_out, B_prime, C_prime, D_prime;

  not not_1 (A_prime, A);
  not not_2 (B_prime, B);
  not not_3 (C_prime, C);
  _7_Segment_Display u_7_segment_display_1 (.g(g), .f(f), .a(a_2), .b(b_2), .e(e), .d(d_2), .c(c_2));  // open: dp
  not not_4 (D_prime, D);
  and and_1 (and_1_out, B, D);
  and and_2 (and_2_out, B_prime, D_prime);
  and and_3 (and_3_out, C, D);
  and and_4 (and_4_out, C_prime, D_prime);
  and and_5 (and_5_out, A_prime, B);
  and and_6 (and_6_out, C, D);
  and and_7 (and_7_out, B_prime, D_prime);
  and and_8 (and_8_out, B_prime, C);
  and and_9 (and_9_out, C, D_prime);
  and and_10 (and_10_out, B, C_prime, D);
  or or_1 (a_2, A, C, and_1_out, and_2_out);
  or or_2 (b_2, B_prime, and_3_out, and_4_out);
  or or_3 (c_2, C_prime, and_5_out, and_6_out);
  or or_4 (d_2, A, and_7_out, and_8_out, and_9_out, and_10_out);
  and and_11 (and_11_out, B_prime, D_prime);
  and and_12 (and_12_out, C, D_prime);
  and and_13 (and_13_out, C_prime, D_prime);
  and and_14 (and_14_out, B, C_prime);
  and and_15 (and_15_out, B, D_prime);
  and and_16 (and_16_out, B, C_prime);
  and and_17 (and_17_out, C, D_prime);
  and and_18 (and_18_out, B_prime, C);
  or or_5 (e, and_11_out, and_12_out);
  or or_6 (f, A, and_13_out, and_14_out, and_15_out);
  or or_7 (g, A, and_16_out, and_17_out, and_18_out);

  // Other names for the same wires on the sheet: a_t = a_2; b_t = b_2; c_t = c_2; d_t = d_2
endmodule
